// Logisim project main.circ as structural Verilog: 11 circuits, main circuit am08x24arc-main
module am08x24arc_main (
  input  SEL,
  output [15:0] out_2,
  output [15:0] out_3
);

  wire and_1_out, and_2_out, and_3_out, and_4_out, and_5_out, and_6_out, and_7_out, BADOP, CLOCK,
       comparator_1_eq, comparator_2_eq, DEVICE_ENABLE, DEVICE_SELECT, DEVICE_SRC, GPU_CLOCK,
       GPU_DEVICE_ENABLE, GPU_DEVICE_SELECT, GPU_DEVICE_SRC, INC_PC, n16x_device_selector_1_out_4,
       n16x_device_selector_1_out_5, n16x_device_selector_1_out_6, n16x_device_selector_1_out_7,
       n16x_device_selector_1_out_8, n16x_device_selector_2_out_4, not_1_out;
  wire [3:0] n16bit_decimal_display_controller_1_digit_0, n16bit_decimal_display_controller_1_digit_1,
       n16bit_decimal_display_controller_1_digit_2, n16bit_decimal_display_controller_1_digit_3,
       n16bit_decimal_display_controller_1_digit_4;
  wire [15:0] DATA_BUS, GPU_DATA_BUS, n16x16_led_matrix_1_out_6, n16x16_led_matrix_1_out_7,
       n16x16_led_matrix_1_out_8, n16x16_led_matrix_1_out_9, n16x16_led_matrix_1_out_10,
       n16x16_led_matrix_1_out_11, n16x16_led_matrix_1_out_12, n16x16_led_matrix_1_out_13,
       n16x16_led_matrix_1_out_14, n16x16_led_matrix_1_out_15, n16x16_led_matrix_1_out_16,
       n16x16_led_matrix_1_out_17, n16x16_led_matrix_1_out_18, n16x16_led_matrix_1_out_19,
       n16x16_led_matrix_1_out_20, n16x16_led_matrix_1_out_21, PC, register_1_q, STACK_NEXT, STACK_TOP;
  wire [23:0] INSTRUCTION;

  am08x24arc_cpu am08x24arc_cpu_1 (
    .DATA_BUS_OUT(DATA_BUS), .STACK_TOP(STACK_TOP), .STACK_NEXT(STACK_NEXT), .CLOCK(CLOCK), .INC_PC(INC_PC),
    .HALT(BADOP), .BADOP(BADOP), .DEVICE_SRC(DEVICE_SRC), .SELECT_DEVICE(DEVICE_SELECT),
    .DEVICE_ENABLE(DEVICE_ENABLE), .DATA_BUS_IN(DATA_BUS), .PC(PC), .INSTRUCTION(INSTRUCTION));
  am08x24arc_clock am08x24arc_clock_1 (.HALT(BADOP), .BADOP(BADOP), .CLOCK(CLOCK), .INC_PC(INC_PC));
  _16x_device_selector u_16x_device_selector_1 (
    .DEVICE(DATA_BUS), .DEVICE_SELECT(DEVICE_SELECT), .CLOCK(CLOCK), .out_4(n16x_device_selector_1_out_4),
    .out_5(n16x_device_selector_1_out_5), .out_6(n16x_device_selector_1_out_6),
    .out_7(n16x_device_selector_1_out_7), .out_8(n16x_device_selector_1_out_8));  // open: out_9, out_10, out_11, out_12, out_13, out_14, out_15, out_16, out_17, out_18, out_19
  and and_1 (and_1_out, n16x_device_selector_1_out_4, DEVICE_ENABLE);
  not not_1 (not_1_out, and_1_out);
  and and_2 (and_2_out, n16x_device_selector_1_out_5, DEVICE_ENABLE);
  and and_3 (and_3_out, n16x_device_selector_1_out_6, DEVICE_ENABLE, CLOCK);
  Hex_Digit_Display hex_digit_display_1 (.value(n16bit_decimal_display_controller_1_digit_4));  // open: dp
  _16bit_decimal_display_controller u_16bit_decimal_display_controller_1 (
    .DATA_IN(DATA_BUS), .DIGIT_4(n16bit_decimal_display_controller_1_digit_4),
    .DIGIT_3(n16bit_decimal_display_controller_1_digit_3),
    .DIGIT_2(n16bit_decimal_display_controller_1_digit_2),
    .DIGIT_1(n16bit_decimal_display_controller_1_digit_1),
    .DIGIT_0(n16bit_decimal_display_controller_1_digit_0), .CLOCK(and_4_out));
  and and_4 (and_4_out, n16x_device_selector_1_out_7, DEVICE_ENABLE, CLOCK);
  TTY tty_1 (.data(DATA_BUS[6:0]), .clk(and_3_out), .clr(and_5_out));  // open: we
  and and_5 (and_5_out, and_3_out, comparator_1_eq);
  Comparator #(.width(9)) comparator_1 (.a(DATA_BUS[15:7]), .b({9{1'b1}}), .eq(comparator_1_eq));  // open: gt, lt
  Hex_Digit_Display hex_digit_display_2 (.value(n16bit_decimal_display_controller_1_digit_2));  // open: dp
  Hex_Digit_Display hex_digit_display_3 (.value(n16bit_decimal_display_controller_1_digit_3));  // open: dp
  ROM #(.addrWidth(16), .dataWidth(24), .Select("low")) Instruction_ROM (.addr(PC), .data(INSTRUCTION));
  RAM #(.addrWidth(16), .dataWidth(16), .Select("low")) Ram (
    .addr(STACK_TOP), .data(DATA_BUS), .sel(not_1_out), .clk(CLOCK), .ld(DEVICE_SRC));  // open: clr
  _16x16_led_matrix u_16x16_led_matrix_1 (
    .DATA_IN(DATA_BUS), .ADRESS(STACK_TOP), .BLOCK(and_2_out), .CLOCK(CLOCK),
    .out_6(n16x16_led_matrix_1_out_6), .out_7(n16x16_led_matrix_1_out_7), .out_8(n16x16_led_matrix_1_out_8),
    .out_9(n16x16_led_matrix_1_out_9), .out_10(n16x16_led_matrix_1_out_10),
    .out_11(n16x16_led_matrix_1_out_11), .out_12(n16x16_led_matrix_1_out_12),
    .out_13(n16x16_led_matrix_1_out_13), .out_14(n16x16_led_matrix_1_out_14),
    .out_15(n16x16_led_matrix_1_out_15), .out_16(n16x16_led_matrix_1_out_16),
    .out_17(n16x16_led_matrix_1_out_17), .out_18(n16x16_led_matrix_1_out_18),
    .out_19(n16x16_led_matrix_1_out_19), .out_20(n16x16_led_matrix_1_out_20),
    .out_21(n16x16_led_matrix_1_out_21), .SEL(SEL));
  DotMatrix #(.inputtype("row"), .matrixcols(16), .matrixrows(16)) dotmatrix_1 (
    .row0(n16x16_led_matrix_1_out_6), .row1(n16x16_led_matrix_1_out_7), .row2(n16x16_led_matrix_1_out_8),
    .row3(n16x16_led_matrix_1_out_9), .row4(n16x16_led_matrix_1_out_10), .row5(n16x16_led_matrix_1_out_11),
    .row6(n16x16_led_matrix_1_out_12), .row7(n16x16_led_matrix_1_out_13), .row8(n16x16_led_matrix_1_out_14),
    .row9(n16x16_led_matrix_1_out_15), .row10(n16x16_led_matrix_1_out_16),
    .row11(n16x16_led_matrix_1_out_17), .row12(n16x16_led_matrix_1_out_18),
    .row13(n16x16_led_matrix_1_out_19), .row14(n16x16_led_matrix_1_out_20), .row15(n16x16_led_matrix_1_out_21));
  Hex_Digit_Display hex_digit_display_4 (.value(n16bit_decimal_display_controller_1_digit_1));  // open: dp
  Hex_Digit_Display hex_digit_display_5 (.value(n16bit_decimal_display_controller_1_digit_0));  // open: dp
  Comparator #(.width(16), .mode("unsigned")) comparator_2 (
    .a(STACK_TOP), .b({16{1'b1}}), .eq(comparator_2_eq));  // open: gt, lt
  am08x24arc_gpu_main_core am08x24arc_gpu_main_core_1 (
    .out_4(GPU_CLOCK), .out_5(out_3), .out_3(out_2), .out_2(GPU_DATA_BUS), .out_6(GPU_DEVICE_SELECT),
    .out_7(GPU_DEVICE_SRC), .out_8(GPU_DEVICE_ENABLE), .in_1(GPU_DATA_BUS));
  and and_6 (and_6_out, n16x_device_selector_1_out_8, CLOCK, comparator_2_eq, DEVICE_ENABLE);
  Register #(.width(16), .Select("low")) register_1 (.D(DATA_BUS), .Q(register_1_q), .clk(and_6_out));  // open: en, clr
  assign GPU_DATA_BUS = and_7_out ? register_1_q : 16'bz;  // Controlled_Buffer controlled_buffer_1
  and and_7 (and_7_out, n16x_device_selector_2_out_4, GPU_DEVICE_SRC, GPU_DEVICE_ENABLE);
  _16x_device_selector u_16x_device_selector_2 (
    .DEVICE(GPU_DATA_BUS), .DEVICE_SELECT(GPU_DEVICE_SELECT), .CLOCK(GPU_CLOCK),
    .out_4(n16x_device_selector_2_out_4));  // open: out_5, out_6, out_7, out_8, out_9, out_10, out_11, out_12, out_13, out_14, out_15, out_16, out_17, out_18, out_19
  DotMatrix #(.inputtype("row"), .matrixcols(32), .matrixrows(32)) dotmatrix_2 ();  // open: row0, row1, row2, row3, row4, row5, row6, row7, row8, row9, row10, row11, row12, row13, row14, row15, row16, row17, row18, row19, row20, row21, row22, row23, row24, row25, row26, row27, row28, row29, row30, row31

  // Other names for the same wires on the sheet: HALT = BADOP

  // Notes on the sheet:
  //   am08x24arc-main
  //   contents of Instruction_ROM (hex, n*v repeats v):
  //   80001 200004 40ffff 40ffff 870400 808000 808000
endmodule

module am08x24arc_cpu (
  input  CLOCK,
  input  INC_PC,
  input  [15:0] DATA_BUS_IN,
  input  [23:0] INSTRUCTION,
  output [15:0] DATA_BUS_OUT,
  output HALT,
  output BADOP,
  output [15:0] STACK_TOP,
  output [15:0] PC,
  output [15:0] STACK_NEXT,
  output SELECT_DEVICE,
  output DEVICE_SRC,
  output DEVICE_ENABLE
);

  wire ALU_SRC, and_1_out, and_2_out, and_3_out, and_4_out, and_5_out, comparator_1_eq, comparator_1_gt,
       comparator_1_lt, JNEG, JPOS, JZ, not_1_out, OPERAND_SRC, or_2_out, PC_ADRESS_WRITE, PC_SRC,
       STACK_NEXT_SRC, STACK_POP, STACK_SWAP, STACK_TOP_SRC;
  wire [3:0] ALU_OP;
  wire [9:3] controlled_buffer_9_out;
  wire [15:0] ALU_OUT, controlled_buffer_1_out, DATA_BUS, STORED_ON_STACK;

  assign controlled_buffer_1_out = INSTRUCTION[23] ? STACK_TOP : 16'bz;  // Controlled_Buffer controlled_buffer_1
  assign controlled_buffer_1_out = ~INSTRUCTION[23] ? DATA_BUS : 16'bz;  // Controlled_Buffer controlled_buffer_2
  and and_1 (and_1_out, INSTRUCTION[23], INSTRUCTION[19], or_2_out);
  and and_2 (and_2_out, ~INSTRUCTION[23], INSTRUCTION[19]);  // AND_Gate
  or or_1 (PC_ADRESS_WRITE, and_2_out, and_1_out);
  // Probe on STACK_TOP
  // Probe on STACK_TOP
  // Probe on STACK_NEXT
  // Probe on STACK_NEXT
  // Probe on STORED_ON_STACK
  Comparator #(.width(16)) comparator_1 (
    .a(STACK_NEXT), .b({16{1'b0}}), .gt(comparator_1_gt), .eq(comparator_1_eq), .lt(comparator_1_lt));
  or or_2 (or_2_out, and_3_out, and_4_out, and_5_out);
  Counter #(.width(16), .max('hffff), .ongoal("stay")) u_PC (
    .load(PC_ADRESS_WRITE), .D(controlled_buffer_1_out), .Q(PC), .clk(INC_PC));  // open: count, carry, clr, preset, down
  and and_3 (and_3_out, comparator_1_gt, JPOS);
  and and_4 (and_4_out, comparator_1_eq, JZ);
  and and_5 (and_5_out, comparator_1_lt, JNEG);
  // Probe on DATA_BUS
  // Probe on INSTRUCTION[15:0]
  // Probe on INSTRUCTION[23:16]
  // Probe on INSTRUCTION[18:16]
  assign DATA_BUS = PC_SRC ? PC : 16'bz;  // Controlled_Buffer controlled_buffer_3
  // Probe on ALU_OUT
  // Probe on ALU_OP
  // Probe on PC
  // Probe on PC
  assign DATA_BUS = OPERAND_SRC ? INSTRUCTION[15:0] : 16'bz;  // Controlled_Buffer controlled_buffer_4
  am08x24arc_cpu_stack am08x24arc_cpu_stack_1 (
    .DATA_IN(DATA_BUS), .PUSH(INSTRUCTION[22]), .POP(STACK_POP), .SWAP(STACK_SWAP), .TOP(STACK_TOP),
    .NEXT(STACK_NEXT), .SEL(1'b0), .CLOCK(CLOCK), .STORED(STORED_ON_STACK));
  assign DATA_BUS_OUT = ~DEVICE_SRC ? DATA_BUS : 16'bz;  // Controlled_Buffer controlled_buffer_5
  assign DATA_BUS = DEVICE_SRC ? DATA_BUS_IN : 16'bz;  // Controlled_Buffer controlled_buffer_6
  nor nor_1 (HALT, INSTRUCTION[16], INSTRUCTION[17], INSTRUCTION[18], INSTRUCTION[19], INSTRUCTION[20], INSTRUCTION[21], INSTRUCTION[22], INSTRUCTION[23]);
  assign DATA_BUS = STACK_TOP_SRC ? STACK_TOP : 16'bz;  // Controlled_Buffer controlled_buffer_7
  assign DATA_BUS = STACK_NEXT_SRC ? STACK_NEXT : 16'bz;  // Controlled_Buffer controlled_buffer_8
  assign {STACK_POP, STACK_SWAP, JZ, JNEG, JPOS, DEVICE_ENABLE, controlled_buffer_9_out[9], ALU_OP[3], controlled_buffer_9_out[7:3], ALU_OP[2:0]} = INSTRUCTION[23] ? INSTRUCTION[15:0] : 16'bz;  // Controlled_Buffer controlled_buffer_9
  Decoder #(.select(3), .enable("false")) decoder_1 (
    .out0(OPERAND_SRC), .out1(DEVICE_SRC), .out2(ALU_SRC), .out3(PC_SRC), .out6(STACK_TOP_SRC),
    .out7(STACK_NEXT_SRC), .sel(INSTRUCTION[18:16]));  // open: out4, out5
  not not_1 (not_1_out, INSTRUCTION[23]);
  assign {STACK_POP, STACK_SWAP, JZ, JNEG, JPOS, DEVICE_ENABLE, controlled_buffer_9_out[9], ALU_OP[3], controlled_buffer_9_out[7:3], ALU_OP[2:0]} = not_1_out ? {16{1'b0}} : 16'bz;  // Controlled_Buffer controlled_buffer_10
  am08x24arc_alu am08x24arc_alu_1 (
    .A(STACK_TOP), .B(STACK_NEXT), .ALU_OP(ALU_OP), .OUT(ALU_OUT));  // open: CARRY_IN, ZF, CF
  assign DATA_BUS = ALU_SRC ? ALU_OUT : 16'bz;  // Controlled_Buffer controlled_buffer_11

  assign BADOP = 1'b0;
  assign SELECT_DEVICE = INSTRUCTION[21];

  // Other names for the same wires on the sheet: ARGUMENT[15:0] = INSTRUCTION[15:0]; OPCODE[7:0] = INSTRUCTION[23:16];
  //   SRC[2:0] = INSTRUCTION[18:16]; PC_t = INSTRUCTION[19]; STACK_PUSH = INSTRUCTION[22];
  //   _24BIT_INSTUCTION = INSTRUCTION[23]; PROGRAM_COUNTER[15:0] = PC

  // Notes on the sheet:
  //   STACK STATUS
  //   PROGRAM COUNTER
  //   Conditional jumps
  //   STATUS
  //   DATA BUS STATUS
  //   INSTRUCTION STATUS
  //   PC STATUS
  //   ALU STATUS
  //   OUTPUT
  //   HALT
  //   STACK
  //   am08x24arc-cpu
  //   DECODER
  //   SOURCE DECODER
  //   ALU
endmodule

module am08x24arc_alu (
  input  [15:0] A,
  input  [15:0] B,
  input  [3:0] ALU_OP,
  input  CARRY_IN,
  output [15:0] OUT,
  output ZF,
  output CF
);

  wire [15:0] adder_1_out, adder_2_out, and_1_out, nand_1_out, negator_1_out, nor_1_out, not_1_out, or_1_out,
       subtractor_1_out, subtractor_2_out, xor_1_out;

  Adder #(.width(16)) adder_1 (.a(A), .b(B), .out(adder_1_out));  // open: cin, cout
  Adder #(.width(16)) adder_2 (.a(A), .b(B), .out(adder_2_out), .cin(CARRY_IN));  // open: cout
  Subtractor #(.width(16)) subtractor_1 (.a(A), .b(B), .out(subtractor_1_out));  // open: bin, bout
  Subtractor #(.width(16)) subtractor_2 (.a(A), .b(B), .out(subtractor_2_out), .bin(CARRY_IN));  // open: bout
  Comparator #(.width(16)) comparator_1 (.a(A), .b(B), .eq(ZF), .lt(CF));  // open: gt
  Negator #(.width(16)) negator_1 (.in(A), .out(negator_1_out));
  assign not_1_out = ~A;  // NOT_Gate not_1, 16 bits wide
  assign and_1_out = A & B;  // AND_Gate and_1, 16 bits wide
  assign or_1_out = A | B;  // OR_Gate or_1, 16 bits wide
  assign nand_1_out = ~(A & B);  // NAND_Gate nand_1, 16 bits wide
  assign nor_1_out = ~(A | B);  // NOR_Gate nor_1, 16 bits wide
  assign xor_1_out = A ^ B;  // XOR_Gate xor_1, 16 bits wide
  Multiplexer #(.select(4), .width(16), .enable("false")) multiplexer_1 (
    .in0(adder_1_out), .in1(adder_2_out), .in2(subtractor_1_out), .in3(subtractor_2_out),
    .in4(negator_1_out), .in5(not_1_out), .in6(and_1_out), .in7(or_1_out), .in8(nand_1_out), .in9(nor_1_out),
    .in10(xor_1_out), .out(OUT), .sel(ALU_OP));  // open: in11, in12, in13, in14, in15

  // Notes on the sheet:
  //   ALU interface
endmodule

module am08x24arc_cpu_stack (
  input  [15:0] DATA_IN,
  input  PUSH,
  input  POP,
  input  SWAP,
  input  SEL,
  input  CLOCK,
  output [15:0] TOP,
  output [15:0] NEXT,
  output [15:0] STORED
);

  wire or_1_out;
  wire [15:0] adder_1_out, multiplexer_1_out, subtractor_1_out;

  _16bit_stack32 u_16bit_stack32_1 (
    .DATA_IN(DATA_IN), .PUSH(PUSH), .POP(POP), .SWAP(SWAP), .TOP(TOP), .NEXT(NEXT), .SEL(SEL), .CLOCK(CLOCK),
    .CARRY_IN({16{1'b0}}));  // open: CARRY_OUT, LAST
  Subtractor #(.width(16)) subtractor_1 (.a(STORED), .b(16'h1), .out(subtractor_1_out));  // open: bin, bout
  Adder #(.width(16)) adder_1 (.a(STORED), .b(16'h1), .out(adder_1_out));  // open: cin, cout
  Multiplexer #(.width(16), .enable("false")) multiplexer_1 (
    .in0(subtractor_1_out), .in1(adder_1_out), .out(multiplexer_1_out), .sel(PUSH));
  Register #(.width(16), .Select("low")) register_1 (
    .D(multiplexer_1_out), .en(or_1_out), .Q(STORED), .clk(CLOCK));  // open: clr
  or or_1 (or_1_out, PUSH, POP);

  // Other names for the same wires on the sheet: POP_OP = POP; PUSH_OP = PUSH; SWAP_OP = SWAP

  // Notes on the sheet:
  //   am08x24arc-stack
endmodule

module am08x24arc_clock (
  input  HALT,
  input  BADOP,
  output CLOCK,
  output INC_PC
);

  wire and_1_out, clock_1_out, not_1_out, t_ff_1_q, t_ff_1_qn, t_ff_2_q, t_ff_2_qn;

  Clock clock_1 (.out(clock_1_out));
  LED led_1 (.in(BADOP));
  and and_1 (and_1_out, clock_1_out, ~HALT, ~BADOP);  // AND_Gate
  not not_1 (not_1_out, and_1_out);
  T_Flip_Flop t_ff_1 (.clk(not_1_out), .T(1'b1), .Q(t_ff_1_q), .Qn(t_ff_1_qn));  // open: preset, reset
  T_Flip_Flop #(.Pre_Clr_Positions("LEGACY"), .enable("true")) t_ff_2 (
    .clk(and_1_out), .T(1'b1), .Q(t_ff_2_q), .Qn(t_ff_2_qn));  // open: preset, reset, en
  and and_2 (CLOCK, and_1_out, t_ff_1_qn, t_ff_2_q);
  and and_3 (INC_PC, t_ff_2_qn, t_ff_1_q, and_1_out);

  // Notes on the sheet:
  //   am08x24arc-clock
endmodule

module am08x24arc_gpu_core (
  input  CLOCK,
  input  INC_PC,
  input  [15:0] DATA_BUS_IN,
  output [15:0] DATA_BUS_OUT,
  output HALT,
  output BADOP,
  output [15:0] STACK_TOP,
  output SELECT_DEVICE,
  output DEVICE_SRC,
  output DEVICE_ENABLE
);

  wire _24BIT_INSTUCTION, ALU_SRC, and_1_out, and_2_out, and_3_out, and_4_out, and_5_out, comparator_1_eq,
       comparator_1_gt, comparator_1_lt, JNEG, JPOS, JZ, not_1_out, OPERAND_SRC, or_2_out, PC_ADRESS_WRITE,
       PC_SRC, STACK_NEXT_SRC, STACK_POP, STACK_SWAP, STACK_TOP_SRC;
  wire [3:0] ALU_OP;
  wire [9:3] controlled_buffer_7_out;
  wire [15:0] ALU_OUT, ARGUMENT, controlled_buffer_1_out, DATA_BUS, PROGRAM_COUNTER, STACK_NEXT;
  wire [22:16] INSTRUCTION;

  assign controlled_buffer_1_out = _24BIT_INSTUCTION ? STACK_TOP : 16'bz;  // Controlled_Buffer controlled_buffer_1
  assign controlled_buffer_1_out = ~_24BIT_INSTUCTION ? DATA_BUS : 16'bz;  // Controlled_Buffer controlled_buffer_2
  and and_1 (and_1_out, _24BIT_INSTUCTION, INSTRUCTION[19], or_2_out);
  and and_2 (and_2_out, ~_24BIT_INSTUCTION, INSTRUCTION[19]);  // AND_Gate
  or or_1 (PC_ADRESS_WRITE, and_2_out, and_1_out);
  Comparator #(.width(16)) comparator_1 (
    .a(STACK_NEXT), .b({16{1'b0}}), .gt(comparator_1_gt), .eq(comparator_1_eq), .lt(comparator_1_lt));
  or or_2 (or_2_out, and_3_out, and_4_out, and_5_out);
  Counter #(.width(16), .max('hffff), .ongoal("stay")) PC (
    .load(PC_ADRESS_WRITE), .D(controlled_buffer_1_out), .Q(PROGRAM_COUNTER), .clk(INC_PC));  // open: count, carry, clr, preset, down
  and and_3 (and_3_out, comparator_1_gt, JPOS);
  and and_4 (and_4_out, comparator_1_eq, JZ);
  assign DATA_BUS_OUT = ~DEVICE_SRC ? DATA_BUS : 16'bz;  // Controlled_Buffer controlled_buffer_3
  assign DATA_BUS = DEVICE_SRC ? DATA_BUS_IN : 16'bz;  // Controlled_Buffer controlled_buffer_4
  and and_5 (and_5_out, comparator_1_lt, JNEG);
  assign DATA_BUS = PC_SRC ? PROGRAM_COUNTER : 16'bz;  // Controlled_Buffer controlled_buffer_5
  Decoder #(.select(3), .enable("false")) decoder_1 (
    .out0(OPERAND_SRC), .out1(DEVICE_SRC), .out2(ALU_SRC), .out3(PC_SRC), .out6(STACK_TOP_SRC),
    .out7(STACK_NEXT_SRC), .sel(INSTRUCTION[18:16]));  // open: out4, out5
  nor nor_1 (HALT, INSTRUCTION[16], INSTRUCTION[17], INSTRUCTION[18], INSTRUCTION[19], INSTRUCTION[20], SELECT_DEVICE, INSTRUCTION[22], _24BIT_INSTUCTION);
  assign DATA_BUS = OPERAND_SRC ? ARGUMENT : 16'bz;  // Controlled_Buffer controlled_buffer_6
  ROM #(.addrWidth(16), .dataWidth(24), .Select("low")) Instruction_ROM (
    .addr(PROGRAM_COUNTER),
    .data({_24BIT_INSTUCTION, INSTRUCTION[22], SELECT_DEVICE, INSTRUCTION[20:16], ARGUMENT}));
  assign {STACK_POP, STACK_SWAP, JZ, JNEG, JPOS, DEVICE_ENABLE, controlled_buffer_7_out[9], ALU_OP[3], controlled_buffer_7_out[7:3], ALU_OP[2:0]} = _24BIT_INSTUCTION ? ARGUMENT : 16'bz;  // Controlled_Buffer controlled_buffer_7
  am08x24arc_gpu_stack am08x24arc_gpu_stack_1 (
    .DATA_IN(DATA_BUS), .PUSH(INSTRUCTION[22]), .POP(STACK_POP), .SWAP(STACK_SWAP), .TOP(STACK_TOP),
    .NEXT(STACK_NEXT), .SEL(1'b0), .CLOCK(CLOCK));
  not not_1 (not_1_out, _24BIT_INSTUCTION);
  assign {STACK_POP, STACK_SWAP, JZ, JNEG, JPOS, DEVICE_ENABLE, controlled_buffer_7_out[9], ALU_OP[3], controlled_buffer_7_out[7:3], ALU_OP[2:0]} = not_1_out ? {16{1'b0}} : 16'bz;  // Controlled_Buffer controlled_buffer_8
  assign DATA_BUS = STACK_NEXT_SRC ? STACK_NEXT : 16'bz;  // Controlled_Buffer controlled_buffer_9
  assign DATA_BUS = STACK_TOP_SRC ? STACK_TOP : 16'bz;  // Controlled_Buffer controlled_buffer_10
  am08x24arc_alu am08x24arc_alu_1 (
    .A(STACK_TOP), .B(STACK_NEXT), .ALU_OP(ALU_OP), .OUT(ALU_OUT));  // open: CARRY_IN, ZF, CF
  assign DATA_BUS = ALU_SRC ? ALU_OUT : 16'bz;  // Controlled_Buffer controlled_buffer_11

  assign BADOP = 1'b0;

  // Other names for the same wires on the sheet: INSTRUCTION (some bits) = {_24BIT_INSTUCTION, SELECT_DEVICE, ARGUMENT};
  //   OPCODE[7:0] = {_24BIT_INSTUCTION, INSTRUCTION[22], SELECT_DEVICE, INSTRUCTION[20:16]};
  //   SRC[2:0] = INSTRUCTION[18:16]; PC = INSTRUCTION[19]; STACK_PUSH = INSTRUCTION[22]

  // Notes on the sheet:
  //   OUTPUT
  //   PROGRAM COUNTER
  //   Conditional jumps
  //   HALT
  //   SOURCE DECODER
  //   contents of Instruction_ROM (hex, n*v repeats v):
  //   400001 c10400
  //   am08x24arc-gpu-core
  //   DECODER
  //   STACK
  //   ALU
endmodule

module am08x24arc_gpu_stack (
  input  [15:0] DATA_IN,
  input  PUSH,
  input  POP,
  input  SWAP,
  input  SEL,
  input  CLOCK,
  output [15:0] TOP,
  output [15:0] NEXT
);

  _16bit_stack8 u_16bit_stack8_1 (
    .DATA_IN(DATA_IN), .PUSH(PUSH), .POP(POP), .SWAP(SWAP), .TOP(TOP), .NEXT(NEXT), .SEL(SEL), .CLOCK(CLOCK),
    .CARRY_IN({16{1'b0}}));  // open: CARRY_OUT, LAST

  // Other names for the same wires on the sheet: POP_OP = POP; PUSH_OP = PUSH; SWAP_OP = SWAP

  // Notes on the sheet:
  //   am08x24arc-gpu-stack
endmodule

module am08x24arc_gpu_main_core (
  input  [15:0] in_1,
  output [15:0] out_2,
  output [15:0] out_3,
  output out_4,
  output [15:0] out_5,
  output out_6,
  output out_7,
  output out_8
);

  wire BADOP, HALT, INC_PC;
  wire [15:0] PC;
  wire [23:0] INSTRUCTION;

  am08x24arc_cpu am08x24arc_cpu_1 (
    .DATA_BUS_OUT(out_2), .STACK_TOP(out_3), .STACK_NEXT(out_5), .CLOCK(out_4), .INC_PC(INC_PC), .HALT(HALT),
    .BADOP(BADOP), .DEVICE_SRC(out_7), .SELECT_DEVICE(out_6), .DEVICE_ENABLE(out_8), .DATA_BUS_IN(in_1),
    .PC(PC), .INSTRUCTION(INSTRUCTION));
  am08x24arc_clock am08x24arc_clock_1 (.HALT(HALT), .BADOP(BADOP), .CLOCK(out_4), .INC_PC(INC_PC));
  ROM #(.addrWidth(16), .dataWidth(24), .Select("low")) Instruction_ROM (.addr(PC), .data(INSTRUCTION));

  // Other names for the same wires on the sheet: CLOCK = out_4; DATA_BUS_IN[15:0] = in_1; DATA_BUS_OUT[15:0] = out_2;
  //   DEVICE_ENABLE = out_8; DEVICE_SELECT = out_6; DEVICE_SRC = out_7; STACK_NEXT[15:0] = out_5;
  //   STACK_TOP[15:0] = out_3

  // Notes on the sheet:
  //   am08x24arc-gpu-main-core
  //   contents of Instruction_ROM (hex, n*v repeats v):
  //   80001 200000 40000a c10400 804000 808000 40000b 8e1800 808000 808000 80002 808000
endmodule

module _16bit_decimal_display_controller (
  input  [15:0] DATA_IN,
  input  CLOCK,
  output [3:0] DIGIT_4,
  output [3:0] DIGIT_3,
  output [3:0] DIGIT_2,
  output [3:0] DIGIT_1,
  output [3:0] DIGIT_0
);

  wire [15:0] divider_1_out, divider_2_out, divider_3_out, divider_4_out, register_1_q;
  wire [15:4] divider_1_rem, divider_2_rem, divider_3_rem, divider_4_rem, divider_5_rem;

  Register #(.width(16), .Select("low")) register_1 (.D(DATA_IN), .Q(register_1_q), .clk(CLOCK));  // open: en, clr
  Divider #(.width(16)) divider_1 (
    .a(register_1_q), .b(16'ha), .out(divider_1_out), .upper({16{1'b0}}), .rem({divider_1_rem, DIGIT_0}));
  Divider #(.width(16)) divider_2 (
    .a(divider_1_out), .b(16'ha), .out(divider_2_out), .upper({16{1'b0}}), .rem({divider_2_rem, DIGIT_1}));
  Divider #(.width(16)) divider_3 (
    .a(divider_2_out), .b(16'ha), .out(divider_3_out), .upper({16{1'b0}}), .rem({divider_3_rem, DIGIT_2}));
  Divider #(.width(16)) divider_4 (
    .a(divider_3_out), .b(16'ha), .out(divider_4_out), .upper({16{1'b0}}), .rem({divider_4_rem, DIGIT_3}));
  Divider #(.width(16)) divider_5 (
    .a(divider_4_out), .b(16'ha), .upper({16{1'b0}}), .rem({divider_5_rem, DIGIT_4}));  // open: out
endmodule

module _16x16_led_matrix (
  input  [15:0] DATA_IN,
  input  [15:0] ADRESS,
  input  BLOCK,
  input  CLOCK,
  input  SEL,
  output [15:0] out_6,
  output [15:0] out_7,
  output [15:0] out_8,
  output [15:0] out_9,
  output [15:0] out_10,
  output [15:0] out_11,
  output [15:0] out_12,
  output [15:0] out_13,
  output [15:0] out_14,
  output [15:0] out_15,
  output [15:0] out_16,
  output [15:0] out_17,
  output [15:0] out_18,
  output [15:0] out_19,
  output [15:0] out_20,
  output [15:0] out_21
);

  wire and_1_out, and_2_out, and_3_out, and_4_out, and_5_out, and_6_out, and_7_out, and_8_out, and_9_out,
       and_10_out, and_11_out, and_12_out, and_13_out, and_14_out, and_15_out, and_16_out, decoder_1_out0,
       decoder_1_out1, decoder_1_out2, decoder_1_out3, decoder_1_out4, decoder_1_out5, decoder_1_out6,
       decoder_1_out7, decoder_1_out8, decoder_1_out9, decoder_1_out10, decoder_1_out11, decoder_1_out12,
       decoder_1_out13, decoder_1_out14, decoder_1_out15;

  Decoder #(.select(4), .enable("false")) decoder_1 (
    .out0(decoder_1_out0), .out1(decoder_1_out1), .out2(decoder_1_out2), .out3(decoder_1_out3),
    .out4(decoder_1_out4), .out5(decoder_1_out5), .out6(decoder_1_out6), .out7(decoder_1_out7),
    .out8(decoder_1_out8), .out9(decoder_1_out9), .out10(decoder_1_out10), .out11(decoder_1_out11),
    .out12(decoder_1_out12), .out13(decoder_1_out13), .out14(decoder_1_out14), .out15(decoder_1_out15),
    .sel(ADRESS[3:0]));
  and and_1 (and_1_out, decoder_1_out15, BLOCK);
  and and_2 (and_2_out, decoder_1_out14, BLOCK);
  and and_3 (and_3_out, decoder_1_out13, BLOCK);
  and and_4 (and_4_out, decoder_1_out12, BLOCK);
  and and_5 (and_5_out, decoder_1_out11, BLOCK);
  and and_6 (and_6_out, decoder_1_out10, BLOCK);
  and and_7 (and_7_out, decoder_1_out9, BLOCK);
  and and_8 (and_8_out, decoder_1_out8, BLOCK);
  and and_9 (and_9_out, decoder_1_out7, BLOCK);
  and and_10 (and_10_out, decoder_1_out6, BLOCK);
  and and_11 (and_11_out, decoder_1_out5, BLOCK);
  and and_12 (and_12_out, decoder_1_out4, BLOCK);
  and and_13 (and_13_out, decoder_1_out3, BLOCK);
  and and_14 (and_14_out, decoder_1_out2, BLOCK);
  and and_15 (and_15_out, decoder_1_out1, BLOCK);
  and and_16 (and_16_out, decoder_1_out0, BLOCK);
  Register #(.width(16), .Select("low")) register_1 (
    .D(DATA_IN), .en(and_1_out), .Q(out_6), .clk(CLOCK), .cs(SEL));  // open: clr, preset
  Register #(.width(16), .Select("low")) register_2 (
    .D(DATA_IN), .en(and_2_out), .Q(out_7), .clk(CLOCK), .cs(SEL));  // open: clr, preset
  Register #(.width(16), .Select("low")) register_3 (
    .D(DATA_IN), .en(and_3_out), .Q(out_8), .clk(CLOCK), .cs(SEL));  // open: clr, preset
  Register #(.width(16), .Select("low")) register_4 (
    .D(DATA_IN), .en(and_4_out), .Q(out_9), .clk(CLOCK), .cs(SEL));  // open: clr, preset
  Register #(.width(16), .Select("low")) register_5 (
    .D(DATA_IN), .en(and_5_out), .Q(out_10), .clk(CLOCK), .cs(SEL));  // open: clr, preset
  Register #(.width(16), .Select("low")) register_6 (
    .D(DATA_IN), .en(and_6_out), .Q(out_11), .clk(CLOCK), .cs(SEL));  // open: clr, preset
  Register #(.width(16), .Select("low")) register_7 (
    .D(DATA_IN), .en(and_7_out), .Q(out_12), .clk(CLOCK), .cs(SEL));  // open: clr, preset
  Register #(.width(16), .Select("low")) register_8 (
    .D(DATA_IN), .en(and_8_out), .Q(out_13), .clk(CLOCK), .cs(SEL));  // open: clr, preset
  Register #(.width(16), .Select("low")) register_9 (
    .D(DATA_IN), .en(and_9_out), .Q(out_14), .clk(CLOCK), .cs(SEL));  // open: clr, preset
  Register #(.width(16), .Select("low")) register_10 (
    .D(DATA_IN), .en(and_10_out), .Q(out_15), .clk(CLOCK), .cs(SEL));  // open: clr, preset
  Register #(.width(16), .Select("low")) register_11 (
    .D(DATA_IN), .en(and_11_out), .Q(out_16), .clk(CLOCK), .cs(SEL));  // open: clr, preset
  Register #(.width(16), .Select("low")) register_12 (
    .D(DATA_IN), .en(and_12_out), .Q(out_17), .clk(CLOCK), .cs(SEL));  // open: clr, preset
  Register #(.width(16), .Select("low")) register_13 (
    .D(DATA_IN), .en(and_13_out), .Q(out_18), .clk(CLOCK), .cs(SEL));  // open: clr, preset
  Register #(.width(16), .Select("low")) register_14 (
    .D(DATA_IN), .en(and_14_out), .Q(out_19), .clk(CLOCK), .cs(SEL));  // open: clr, preset
  Register #(.width(16), .Select("low")) register_15 (
    .D(DATA_IN), .en(and_15_out), .Q(out_20), .clk(CLOCK), .cs(SEL));  // open: clr, preset
  Register #(.width(16), .Select("low")) register_16 (
    .D(DATA_IN), .en(and_16_out), .Q(out_21), .clk(CLOCK), .cs(SEL));  // open: clr, preset

  // Other names for the same wires on the sheet: DATA_BUS[15:0] = DATA_IN
endmodule

module _16x_device_selector (
  input  [15:0] DEVICE,
  input  DEVICE_SELECT,
  input  CLOCK,
  output out_4,
  output out_5,
  output out_6,
  output out_7,
  output out_8,
  output out_9,
  output out_10,
  output out_11,
  output out_12,
  output out_13,
  output out_14,
  output out_15,
  output out_16,
  output out_17,
  output out_18,
  output out_19
);

  wire and_1_out;
  wire [15:0] register_1_q;

  and and_1 (and_1_out, CLOCK, DEVICE_SELECT);
  Register #(.width(16), .Select("low")) register_1 (.D(DEVICE), .Q(register_1_q), .clk(and_1_out));  // open: en, clr
  Decoder #(.select(4), .enable("false")) decoder_1 (
    .out0(out_4), .out1(out_5), .out2(out_6), .out3(out_7), .out4(out_8), .out5(out_9), .out6(out_10),
    .out7(out_11), .out8(out_12), .out9(out_13), .out10(out_14), .out11(out_15), .out12(out_16),
    .out13(out_17), .out14(out_18), .out15(out_19), .sel(register_1_q[3:0]));
endmodule
